# Fritzing sketch p17_piezoelettrico_a_due_tocchi_e_led (saved by Fritzing 0.9.3b)
breadboards: 1

parts:
  Componente1 = Arduino Uno (Rev3)
  R1 = Resistor [tolerance=±5% resistance=220 package=THT]
  R3 = Resistor [tolerance=±5% resistance=220 package=THT]
  LED1 = LED - 5mm [color="Red (633nm)" package="5 mm [THT]"]
  J1 = Piezo Speaker

nets:
  N1: Componente1.A0, J1.pin1
  N2: Componente1.D13/SCK, R1.Pin_1
  N3: Componente1.GND, R3.Pin_1, LED1.cathode
  N4: R1.Pin_0, LED1.anode
  N5: R3.Pin_0, J1.pin2
